# Fritzing sketch Mecanomiograma (saved by Fritzing 0.9.2b)
circuit board: 8.21264cm x 4.66944cm
breadboards: 1

parts:
  Parte1 = Arduino Pro Mini v13
  J1 = female pin header, 10 pins [form="♀ (female)"]
  J2 = female pin header, 3 pins [form="♀ (female)"]
  J3 = screw terminal, 2 pins
  D1 = Rectifier Diode [part_number=1N4001 package="300 mil [THT]"]
  C1 = Electrolytic Capacitor [capacitance=1µF package="100 mil [THT, electrolytic]"]  # not connected
  C2 = Ceramic Capacitor [capacitance=100nF package="100 mil [THT, multilayer]"]  # not connected
  U1 = LM 358 Dual Op-Amp [package="DIP8 [THT]"]
  U2 = LM 358 Dual Op-Amp [package="DIP8 [THT]"]
  U3 = LM 358 Dual Op-Amp [package="DIP8 [THT]"]
  J4 = female pin header, 3 pins [form="♀ (female)"]
  R1 = Resistor [tolerance=±5% resistance=220k package=THT]
  R2 = Resistor [tolerance=±5% resistance=220k package=THT]
  16_9K = TRIMPOT [package=trim_pot_pth]
  R4 = Resistor [tolerance=±5% resistance=1k package=THT]
  R5 = Resistor [tolerance=±5% resistance=2k package=THT]
  J5 = screw terminal, 2 pins
  R6 = Resistor [tolerance=±5% resistance=220 package=THT]
  C3 = Electrolytic Capacitor [capacitance=1µF package="100 mil [THT, electrolytic]"]
  R7 = Resistor [tolerance=±5% resistance=2k package=THT]
  R8 = Resistor [tolerance=±5% resistance=12k package=THT]
  C4 = Ceramic Capacitor [capacitance=100nF package="100 mil [THT, multilayer]"]
  8_87K = TRIMPOT [package=trim_pot_pth]
  18_87K = TRIMPOT [package=trim_pot_pth]
  C5 = Ceramic Capacitor [capacitance=100nF package="100 mil [THT, multilayer]"]
  C7 = Ceramic Capacitor [capacitance=100nF package="100 mil [THT, multilayer]"]
  6_98K = TRIMPOT [package=trim_pot_pth]
  3_48K = TRIMPOT [package=trim_pot_pth]
  560nF = Ceramic Capacitor [capacitance=100nF package="100 mil [THT, multilayer]"]
  C9 = Ceramic Capacitor [capacitance=100nF package="100 mil [THT, multilayer]"]

nets:
  N1: Parte1.VCC, J1.pin10, D1.cathode, U1.connector7, R1.Pin_1
  N2: Parte1.GND, J1.pin9, J2.pin3, J3.pin1, U1.connector3, U2.connector3, U3.connector3, J5.pin1, C4.0, C7.0, C9.1
  N3: Parte1.A4, J1.pin7
  N4: Parte1.A5, J1.pin8
  N5: Parte1.A3, J4.pin3
  N6: Parte1.A2, J4.pin2
  N7: Parte1.A1, J4.pin1
  N8: Parte1.A0, U3.connector5, U3.connector6, 560nF.0
  N9: Parte1.D9_PWM, J2.pin1
  N10: J2.pin2, J3.pin2, D1.anode
  N11: U1.connector0, R4.Pin_0
  N12: U1.connector1, R4.Pin_1, R5.Pin_0
  N13: U1.connector2, R1.Pin_0, R2.Pin_1
  N14: U2.connector0, 16_9K.WIPER, R8.Pin_1
  N15: U2.connector1, R7.Pin_1, R8.Pin_0
  N16: U2.connector2, R5.Pin_1
  N17: U2.connector4, 16_9K.CCW, C4.1
  N18: U2.connector5, U2.connector6, 8_87K.WIPER
  N19: U2.connector7, U3.connector7, R6.Pin_1
  N20: U3.connector0, U3.connector1, C5.0
  N21: U3.connector2, 18_87K.CCW, C7.1
  N22: U3.connector4, 6_98K.CCW, C9.0
  N23: J5.pin2, R6.Pin_0, C3.+
  N24: C3.-, R7.Pin_0
  N25: 8_87K.CCW, 18_87K.WIPER, C5.1
  N26: 6_98K.WIPER, 3_48K.WIPER, 560nF.1
