# Fritzing sketch Sensor muscular_arduino (saved by Fritzing 0.9.2b)
circuit board: 8.75384cm x 4.43113cm
breadboards: 1

parts:
  U1 = LM 358 Dual Op-Amp [package="DIP8 [THT]"]
  LED1 = LED - 5mm [color="Red (633nm)" package="5 mm [THT]"]
  LED2 = LED - 5mm [color="Red (633nm)" package="5 mm [THT]"]
  R1 = Resistor [tolerance=±5% resistance=220 package=THT]
  R2 = Resistor [tolerance=±5% resistance=220 package=THT]
  C1 = Electrolytic Capacitor [capacitance=1µF package="100 mil [THT, electrolytic]"]
  R3 = Resistor [tolerance=±5% resistance=220 package=THT]
  R4 = Resistor [tolerance=±5% resistance=220 package=THT]
  R5 = Resistor [tolerance=±5% resistance=220 package=THT]
  POT1 = Breadboard Trimpot
  C3 = Electrolytic Capacitor [capacitance=1µF package="100 mil [THT, electrolytic]"]
  R6 = Resistor [tolerance=±5% resistance=220 package=THT]
  R7 = Resistor [tolerance=±5% resistance=220 package=THT]
  R8 = Resistor [tolerance=±5% resistance=220 package=THT]
  Parte2 = Arduino Pro Mini v13
  J5 = female pin header, 10 pins [form="♀ (female)"]
  J6 = female pin header, 3 pins [form="♀ (female)"]
  J7 = screw terminal, 2 pins
  D2 = Rectifier Diode [part_number=1N4001 package="300 mil [THT]"]
  C5 = Electrolytic Capacitor [capacitance=1µF package="100 mil [THT, electrolytic]"]  # not connected
  C6 = Ceramic Capacitor [capacitance=100nF package="100 mil [THT, multilayer]"]  # not connected
  J8 = female pin header, 3 pins [form="♀ (female)"]
  C4 = Tantalum Capacitor [capacitance=1µF package="200 mil [THT, tantalum]"]
  C2 = Tantalum Capacitor [capacitance=1µF package="100 mil [THT, tantalum]"]

nets:
  N1: U1.connector0, R5.Pin_0, POT1.PIN2, C2.-
  N2: U1.connector1, R4.Pin_0, R5.Pin_1, C2.+
  N3: U1.connector2, C1.+, R3.Pin_0
  N4: U1.connector3, LED1.anode, LED2.anode, R3.Pin_1, R4.Pin_1, POT1.PIN1, R6.Pin_1, R7.Pin_0, Parte2.GND, J5.pin9, J6.pin3, J7.pin1
  N5: U1.connector4, C3.-, R6.Pin_0
  N6: U1.connector5, R7.Pin_1, R8.Pin_0, C4.-
  N7: U1.connector6, R8.Pin_1, Parte2.A0, C4.+
  N8: U1.connector7, R1.Pin_1, R2.Pin_1, J6.pin2, J7.pin2, D2.anode
  N9: LED1.cathode, R1.Pin_0
  N10: LED2.cathode, R2.Pin_0, C1.-
  N11: POT1.PIN3, C3.+
  N12: Parte2.A4, J5.pin7
  N13: Parte2.A5, J5.pin8
  N14: Parte2.VCC, J5.pin10, D2.cathode
  N15: Parte2.A3, J8.pin3
  N16: Parte2.A2, J8.pin2
  N17: Parte2.A1, J8.pin1
  N18: Parte2.D9_PWM, J6.pin1
